// Logisim project TRABALHO.circ as structural Verilog: 3 circuits, main circuit main
module main (
);

  Registrador registrador_1 ();  // open: a0, a1, a2, a3, a4, a5, a6, a7, a8, a9, a10, a11, a12, a13, a14, a15, a16, a17, a18, a19, a20, a21, a22, a23, a24, a25, a26, a27, a28, a29, a30, a31, W_En, CLK, s0, s1, s2, s3, s4, s5, s6, s7, s8, s9, s10, s11, s12, s13, s14, s15, s16, s17, s18, s19, s20, s21, s22, s23, s24, s25, s26, s27, s28, s29, s30, s31
endmodule

module Registrador (
  input  a0,
  input  a1,
  input  a2,
  input  a3,
  input  a4,
  input  a5,
  input  a6,
  input  a7,
  input  a8,
  input  a9,
  input  a10,
  input  a11,
  input  a12,
  input  a13,
  input  a14,
  input  a15,
  input  a16,
  input  a17,
  input  a18,
  input  a19,
  input  a20,
  input  a21,
  input  a22,
  input  a23,
  input  a24,
  input  a25,
  input  a26,
  input  a27,
  input  a28,
  input  a29,
  input  a30,
  input  a31,
  input  W_En,
  input  CLK,
  output s0,
  output s1,
  output s2,
  output s3,
  output s4,
  output s5,
  output s6,
  output s7,
  output s8,
  output s9,
  output s10,
  output s11,
  output s12,
  output s13,
  output s14,
  output s15,
  output s16,
  output s17,
  output s18,
  output s19,
  output s20,
  output s21,
  output s22,
  output s23,
  output s24,
  output s25,
  output s26,
  output s27,
  output s28,
  output s29,
  output s30,
  output s31
);

  wire multiplexer_1_out, multiplexer_2_out, multiplexer_3_out, multiplexer_4_out, multiplexer_5_out,
       multiplexer_6_out, multiplexer_7_out, multiplexer_8_out, multiplexer_9_out, multiplexer_10_out,
       multiplexer_11_out, multiplexer_12_out, multiplexer_13_out, multiplexer_14_out, multiplexer_15_out,
       multiplexer_16_out, multiplexer_17_out, multiplexer_18_out, multiplexer_19_out, multiplexer_20_out,
       multiplexer_21_out, multiplexer_22_out, multiplexer_23_out, multiplexer_24_out, multiplexer_25_out,
       multiplexer_26_out, multiplexer_27_out, multiplexer_28_out, multiplexer_29_out, multiplexer_30_out,
       multiplexer_31_out, multiplexer_32_out;

  Multiplexer multiplexer_1 (.in0(s0), .in1(a0), .out(multiplexer_1_out), .sel(W_En));
  Multiplexer multiplexer_2 (.in0(s1), .in1(a1), .out(multiplexer_2_out), .sel(W_En));
  Multiplexer multiplexer_3 (.in0(s2), .in1(a2), .out(multiplexer_3_out), .sel(W_En));
  Multiplexer multiplexer_4 (.in0(s3), .in1(a3), .out(multiplexer_4_out), .sel(W_En));
  Multiplexer multiplexer_5 (.in0(s4), .in1(a4), .out(multiplexer_5_out), .sel(W_En));
  Multiplexer multiplexer_6 (.in0(s5), .in1(a5), .out(multiplexer_6_out), .sel(W_En));
  Multiplexer multiplexer_7 (.in0(s6), .in1(a6), .out(multiplexer_7_out), .sel(W_En));
  Multiplexer multiplexer_8 (.in0(s7), .in1(a7), .out(multiplexer_8_out), .sel(W_En));
  Multiplexer multiplexer_9 (.in0(s8), .in1(a8), .out(multiplexer_9_out), .sel(W_En));
  Multiplexer multiplexer_10 (.in0(s9), .in1(a9), .out(multiplexer_10_out), .sel(W_En));
  Multiplexer multiplexer_11 (.in0(s10), .in1(a10), .out(multiplexer_11_out), .sel(W_En));
  Multiplexer multiplexer_12 (.in0(s11), .in1(a11), .out(multiplexer_12_out), .sel(W_En));
  Multiplexer multiplexer_13 (.in0(s12), .in1(a12), .out(multiplexer_13_out), .sel(W_En));
  Multiplexer multiplexer_14 (.in0(s13), .in1(a13), .out(multiplexer_14_out), .sel(W_En));
  Multiplexer multiplexer_15 (.in0(s14), .in1(a14), .out(multiplexer_15_out), .sel(W_En));
  Multiplexer multiplexer_16 (.in0(s15), .in1(a15), .out(multiplexer_16_out), .sel(W_En));
  Multiplexer multiplexer_17 (.in0(s16), .in1(a16), .out(multiplexer_17_out), .sel(W_En));
  Multiplexer multiplexer_18 (.in0(s17), .in1(a17), .out(multiplexer_18_out), .sel(W_En));
  Multiplexer multiplexer_19 (.in0(s18), .in1(a18), .out(multiplexer_19_out), .sel(W_En));
  Multiplexer multiplexer_20 (.in0(s19), .in1(a19), .out(multiplexer_20_out), .sel(W_En));
  Multiplexer multiplexer_21 (.in0(s20), .in1(a20), .out(multiplexer_21_out), .sel(W_En));
  Multiplexer multiplexer_22 (.in0(s21), .in1(a21), .out(multiplexer_22_out), .sel(W_En));
  Multiplexer multiplexer_23 (.in0(s22), .in1(a22), .out(multiplexer_23_out), .sel(W_En));
  Multiplexer multiplexer_24 (.in0(s23), .in1(a23), .out(multiplexer_24_out), .sel(W_En));
  Multiplexer multiplexer_25 (.in0(s24), .in1(a24), .out(multiplexer_25_out), .sel(W_En));
  Multiplexer multiplexer_26 (.in0(s25), .in1(a25), .out(multiplexer_26_out), .sel(W_En));
  Multiplexer multiplexer_27 (.in0(s26), .in1(a26), .out(multiplexer_27_out), .sel(W_En));
  Multiplexer multiplexer_28 (.in0(s27), .in1(a27), .out(multiplexer_28_out), .sel(W_En));
  Multiplexer multiplexer_29 (.in0(s28), .in1(a28), .out(multiplexer_29_out), .sel(W_En));
  Multiplexer multiplexer_30 (.in0(s29), .in1(a29), .out(multiplexer_30_out), .sel(W_En));
  Multiplexer multiplexer_31 (.in0(s30), .in1(a30), .out(multiplexer_31_out), .sel(W_En));
  Multiplexer multiplexer_32 (.in0(s31), .in1(a31), .out(multiplexer_32_out), .sel(W_En));
  D_Flip_Flop d_ff_1 (.D(multiplexer_1_out), .clk(CLK), .Q(s0));  // open: Qn, preset, reset
  D_Flip_Flop d_ff_2 (.D(multiplexer_2_out), .clk(CLK), .Q(s1));  // open: Qn, preset, reset
  D_Flip_Flop d_ff_3 (.D(multiplexer_3_out), .clk(CLK), .Q(s2));  // open: Qn, preset, reset
  D_Flip_Flop d_ff_4 (.D(multiplexer_4_out), .clk(CLK), .Q(s3));  // open: Qn, preset, reset
  D_Flip_Flop d_ff_5 (.D(multiplexer_5_out), .clk(CLK), .Q(s4));  // open: Qn, preset, reset
  D_Flip_Flop d_ff_6 (.D(multiplexer_6_out), .clk(CLK), .Q(s5));  // open: Qn, preset, reset
  D_Flip_Flop d_ff_7 (.D(multiplexer_7_out), .clk(CLK), .Q(s6));  // open: Qn, preset, reset
  D_Flip_Flop d_ff_8 (.D(multiplexer_8_out), .clk(CLK), .Q(s7));  // open: Qn, preset, reset
  D_Flip_Flop d_ff_9 (.D(multiplexer_9_out), .clk(CLK), .Q(s8));  // open: Qn, preset, reset
  D_Flip_Flop d_ff_10 (.D(multiplexer_10_out), .clk(CLK), .Q(s9));  // open: Qn, preset, reset
  D_Flip_Flop d_ff_11 (.D(multiplexer_11_out), .clk(CLK), .Q(s10));  // open: Qn, preset, reset
  D_Flip_Flop d_ff_12 (.D(multiplexer_12_out), .clk(CLK), .Q(s11));  // open: Qn, preset, reset
  D_Flip_Flop d_ff_13 (.D(multiplexer_13_out), .clk(CLK), .Q(s12));  // open: Qn, preset, reset
  D_Flip_Flop d_ff_14 (.D(multiplexer_14_out), .clk(CLK), .Q(s13));  // open: Qn, preset, reset
  D_Flip_Flop d_ff_15 (.D(multiplexer_15_out), .clk(CLK), .Q(s14));  // open: Qn, preset, reset
  D_Flip_Flop d_ff_16 (.D(multiplexer_16_out), .clk(CLK), .Q(s15));  // open: Qn, preset, reset
  D_Flip_Flop d_ff_17 (.D(multiplexer_17_out), .clk(CLK), .Q(s16));  // open: Qn, preset, reset
  D_Flip_Flop d_ff_18 (.D(multiplexer_18_out), .clk(CLK), .Q(s17));  // open: Qn, preset, reset
  D_Flip_Flop d_ff_19 (.D(multiplexer_19_out), .clk(CLK), .Q(s18));  // open: Qn, preset, reset
  D_Flip_Flop d_ff_20 (.D(multiplexer_20_out), .clk(CLK), .Q(s19));  // open: Qn, preset, reset
  D_Flip_Flop d_ff_21 (.D(multiplexer_21_out), .clk(CLK), .Q(s20));  // open: Qn, preset, reset
  D_Flip_Flop d_ff_22 (.D(multiplexer_22_out), .clk(CLK), .Q(s21));  // open: Qn, preset, reset
  D_Flip_Flop d_ff_23 (.D(multiplexer_23_out), .clk(CLK), .Q(s22));  // open: Qn, preset, reset
  D_Flip_Flop d_ff_24 (.D(multiplexer_24_out), .clk(CLK), .Q(s23));  // open: Qn, preset, reset
  D_Flip_Flop d_ff_25 (.D(multiplexer_25_out), .clk(CLK), .Q(s24));  // open: Qn, preset, reset
  D_Flip_Flop d_ff_26 (.D(multiplexer_26_out), .clk(CLK), .Q(s25));  // open: Qn, preset, reset
  D_Flip_Flop d_ff_27 (.D(multiplexer_27_out), .clk(CLK), .Q(s26));  // open: Qn, preset, reset
  D_Flip_Flop d_ff_28 (.D(multiplexer_28_out), .clk(CLK), .Q(s27));  // open: Qn, preset, reset
  D_Flip_Flop d_ff_29 (.D(multiplexer_29_out), .clk(CLK), .Q(s28));  // open: Qn, preset, reset
  D_Flip_Flop d_ff_30 (.D(multiplexer_30_out), .clk(CLK), .Q(s29));  // open: Qn, preset, reset
  D_Flip_Flop d_ff_31 (.D(multiplexer_31_out), .clk(CLK), .Q(s30));  // open: Qn, preset, reset
  D_Flip_Flop d_ff_32 (.D(multiplexer_32_out), .clk(CLK), .Q(s31));  // open: Qn, preset, reset
endmodule

module Banco_de_registradores (
  input  CLK
);

  wire undriven, undriven_2, undriven_3, undriven_4, undriven_5, undriven_6, undriven_7, undriven_8,
       undriven_9, undriven_10, undriven_11, undriven_12, undriven_13, undriven_14, undriven_15, undriven_16,
       undriven_17, undriven_18, undriven_19, undriven_20, undriven_21, undriven_22, undriven_23,
       undriven_24, undriven_25, undriven_26, undriven_27, undriven_28, undriven_29;
  wire [31:0] registrador_1_s0, registrador_2_s0, registrador_3_s0, registrador_4_s0, registrador_5_s0,
       registrador_6_s0, registrador_7_s0, registrador_8_s0, registrador_9_s0, registrador_10_s0,
       registrador_11_s0, registrador_12_s0, registrador_13_s0, registrador_14_s0, registrador_15_s0,
       registrador_16_s0, undriven_30, undriven_31, undriven_32, undriven_33, undriven_34, undriven_35,
       undriven_36, undriven_37, undriven_38, undriven_39, undriven_40, undriven_41, undriven_42,
       undriven_43, undriven_44, undriven_45;

  Registrador registrador_1 (
    .a0(undriven_30[0]), .a1(undriven_30[1]), .a2(undriven_30[2]), .a3(undriven_30[3]), .a4(undriven_30[4]),
    .a5(undriven_30[5]), .a6(undriven_30[6]), .a7(undriven_30[7]), .a8(undriven_30[8]), .a9(undriven_30[9]),
    .a10(undriven_30[10]), .a11(undriven_30[11]), .a12(undriven_30[12]), .a13(undriven_30[13]),
    .a14(undriven_30[14]), .a15(undriven_30[15]), .a16(undriven_30[16]), .a17(undriven_30[17]),
    .a18(undriven_30[18]), .a19(undriven_30[19]), .a20(undriven_30[20]), .a21(undriven_30[21]),
    .a22(undriven_30[22]), .a23(undriven_30[23]), .a24(undriven_30[24]), .a25(undriven_30[25]),
    .a26(undriven_30[26]), .a27(undriven_30[27]), .a28(undriven_30[28]), .a29(undriven_30[29]),
    .a30(undriven_30[30]), .a31(undriven_30[31]), .CLK(undriven), .s0(registrador_1_s0[0]),
    .s1(registrador_1_s0[1]), .s2(registrador_1_s0[2]), .s3(registrador_1_s0[3]), .s4(registrador_1_s0[4]),
    .s5(registrador_1_s0[5]), .s6(registrador_1_s0[6]), .s7(registrador_1_s0[7]), .s8(registrador_1_s0[8]),
    .s9(registrador_1_s0[9]), .s10(registrador_1_s0[10]), .s11(registrador_1_s0[11]),
    .s12(registrador_1_s0[12]), .s13(registrador_1_s0[13]), .s14(registrador_1_s0[14]),
    .s15(registrador_1_s0[15]), .s16(registrador_1_s0[16]), .s17(registrador_1_s0[17]),
    .s18(registrador_1_s0[18]), .s19(registrador_1_s0[19]), .s20(registrador_1_s0[20]),
    .s21(registrador_1_s0[21]), .s22(registrador_1_s0[22]), .s23(registrador_1_s0[23]),
    .s24(registrador_1_s0[24]), .s25(registrador_1_s0[25]), .s26(registrador_1_s0[26]),
    .s27(registrador_1_s0[27]), .s28(registrador_1_s0[28]), .s29(registrador_1_s0[29]),
    .s30(registrador_1_s0[30]), .s31(registrador_1_s0[31]));  // open: W_En
  Registrador registrador_2 (
    .a0(undriven_31[0]), .a1(undriven_31[1]), .a2(undriven_31[2]), .a3(undriven_31[3]), .a4(undriven_31[4]),
    .a5(undriven_31[5]), .a6(undriven_31[6]), .a7(undriven_31[7]), .a8(undriven_31[8]), .a9(undriven_31[9]),
    .a10(undriven_31[10]), .a11(undriven_31[11]), .a12(undriven_31[12]), .a13(undriven_31[13]),
    .a14(undriven_31[14]), .a15(undriven_31[15]), .a16(undriven_31[16]), .a17(undriven_31[17]),
    .a18(undriven_31[18]), .a19(undriven_31[19]), .a20(undriven_31[20]), .a21(undriven_31[21]),
    .a22(undriven_31[22]), .a23(undriven_31[23]), .a24(undriven_31[24]), .a25(undriven_31[25]),
    .a26(undriven_31[26]), .a27(undriven_31[27]), .a28(undriven_31[28]), .a29(undriven_31[29]),
    .a30(undriven_31[30]), .a31(undriven_31[31]), .CLK(undriven_2), .s0(registrador_2_s0[0]),
    .s1(registrador_2_s0[1]), .s2(registrador_2_s0[2]), .s3(registrador_2_s0[3]), .s4(registrador_2_s0[4]),
    .s5(registrador_2_s0[5]), .s6(registrador_2_s0[6]), .s7(registrador_2_s0[7]), .s8(registrador_2_s0[8]),
    .s9(registrador_2_s0[9]), .s10(registrador_2_s0[10]), .s11(registrador_2_s0[11]),
    .s12(registrador_2_s0[12]), .s13(registrador_2_s0[13]), .s14(registrador_2_s0[14]),
    .s15(registrador_2_s0[15]), .s16(registrador_2_s0[16]), .s17(registrador_2_s0[17]),
    .s18(registrador_2_s0[18]), .s19(registrador_2_s0[19]), .s20(registrador_2_s0[20]),
    .s21(registrador_2_s0[21]), .s22(registrador_2_s0[22]), .s23(registrador_2_s0[23]),
    .s24(registrador_2_s0[24]), .s25(registrador_2_s0[25]), .s26(registrador_2_s0[26]),
    .s27(registrador_2_s0[27]), .s28(registrador_2_s0[28]), .s29(registrador_2_s0[29]),
    .s30(registrador_2_s0[30]), .s31(registrador_2_s0[31]));  // open: W_En
  Registrador registrador_3 (
    .a0(undriven_32[0]), .a1(undriven_32[1]), .a2(undriven_32[2]), .a3(undriven_32[3]), .a4(undriven_32[4]),
    .a5(undriven_32[5]), .a6(undriven_32[6]), .a7(undriven_32[7]), .a8(undriven_32[8]), .a9(undriven_32[9]),
    .a10(undriven_32[10]), .a11(undriven_32[11]), .a12(undriven_32[12]), .a13(undriven_32[13]),
    .a14(undriven_32[14]), .a15(undriven_32[15]), .a16(undriven_32[16]), .a17(undriven_32[17]),
    .a18(undriven_32[18]), .a19(undriven_32[19]), .a20(undriven_32[20]), .a21(undriven_32[21]),
    .a22(undriven_32[22]), .a23(undriven_32[23]), .a24(undriven_32[24]), .a25(undriven_32[25]),
    .a26(undriven_32[26]), .a27(undriven_32[27]), .a28(undriven_32[28]), .a29(undriven_32[29]),
    .a30(undriven_32[30]), .a31(undriven_32[31]), .W_En(undriven_16), .CLK(undriven_3),
    .s0(registrador_3_s0[0]), .s1(registrador_3_s0[1]), .s2(registrador_3_s0[2]), .s3(registrador_3_s0[3]),
    .s4(registrador_3_s0[4]), .s5(registrador_3_s0[5]), .s6(registrador_3_s0[6]), .s7(registrador_3_s0[7]),
    .s8(registrador_3_s0[8]), .s9(registrador_3_s0[9]), .s10(registrador_3_s0[10]),
    .s11(registrador_3_s0[11]), .s12(registrador_3_s0[12]), .s13(registrador_3_s0[13]),
    .s14(registrador_3_s0[14]), .s15(registrador_3_s0[15]), .s16(registrador_3_s0[16]),
    .s17(registrador_3_s0[17]), .s18(registrador_3_s0[18]), .s19(registrador_3_s0[19]),
    .s20(registrador_3_s0[20]), .s21(registrador_3_s0[21]), .s22(registrador_3_s0[22]),
    .s23(registrador_3_s0[23]), .s24(registrador_3_s0[24]), .s25(registrador_3_s0[25]),
    .s26(registrador_3_s0[26]), .s27(registrador_3_s0[27]), .s28(registrador_3_s0[28]),
    .s29(registrador_3_s0[29]), .s30(registrador_3_s0[30]), .s31(registrador_3_s0[31]));
  Registrador registrador_4 (
    .a0(undriven_33[0]), .a1(undriven_33[1]), .a2(undriven_33[2]), .a3(undriven_33[3]), .a4(undriven_33[4]),
    .a5(undriven_33[5]), .a6(undriven_33[6]), .a7(undriven_33[7]), .a8(undriven_33[8]), .a9(undriven_33[9]),
    .a10(undriven_33[10]), .a11(undriven_33[11]), .a12(undriven_33[12]), .a13(undriven_33[13]),
    .a14(undriven_33[14]), .a15(undriven_33[15]), .a16(undriven_33[16]), .a17(undriven_33[17]),
    .a18(undriven_33[18]), .a19(undriven_33[19]), .a20(undriven_33[20]), .a21(undriven_33[21]),
    .a22(undriven_33[22]), .a23(undriven_33[23]), .a24(undriven_33[24]), .a25(undriven_33[25]),
    .a26(undriven_33[26]), .a27(undriven_33[27]), .a28(undriven_33[28]), .a29(undriven_33[29]),
    .a30(undriven_33[30]), .a31(undriven_33[31]), .W_En(undriven_17), .CLK(undriven_4),
    .s0(registrador_4_s0[0]), .s1(registrador_4_s0[1]), .s2(registrador_4_s0[2]), .s3(registrador_4_s0[3]),
    .s4(registrador_4_s0[4]), .s5(registrador_4_s0[5]), .s6(registrador_4_s0[6]), .s7(registrador_4_s0[7]),
    .s8(registrador_4_s0[8]), .s9(registrador_4_s0[9]), .s10(registrador_4_s0[10]),
    .s11(registrador_4_s0[11]), .s12(registrador_4_s0[12]), .s13(registrador_4_s0[13]),
    .s14(registrador_4_s0[14]), .s15(registrador_4_s0[15]), .s16(registrador_4_s0[16]),
    .s17(registrador_4_s0[17]), .s18(registrador_4_s0[18]), .s19(registrador_4_s0[19]),
    .s20(registrador_4_s0[20]), .s21(registrador_4_s0[21]), .s22(registrador_4_s0[22]),
    .s23(registrador_4_s0[23]), .s24(registrador_4_s0[24]), .s25(registrador_4_s0[25]),
    .s26(registrador_4_s0[26]), .s27(registrador_4_s0[27]), .s28(registrador_4_s0[28]),
    .s29(registrador_4_s0[29]), .s30(registrador_4_s0[30]), .s31(registrador_4_s0[31]));
  Registrador registrador_5 (
    .a0(undriven_34[0]), .a1(undriven_34[1]), .a2(undriven_34[2]), .a3(undriven_34[3]), .a4(undriven_34[4]),
    .a5(undriven_34[5]), .a6(undriven_34[6]), .a7(undriven_34[7]), .a8(undriven_34[8]), .a9(undriven_34[9]),
    .a10(undriven_34[10]), .a11(undriven_34[11]), .a12(undriven_34[12]), .a13(undriven_34[13]),
    .a14(undriven_34[14]), .a15(undriven_34[15]), .a16(undriven_34[16]), .a17(undriven_34[17]),
    .a18(undriven_34[18]), .a19(undriven_34[19]), .a20(undriven_34[20]), .a21(undriven_34[21]),
    .a22(undriven_34[22]), .a23(undriven_34[23]), .a24(undriven_34[24]), .a25(undriven_34[25]),
    .a26(undriven_34[26]), .a27(undriven_34[27]), .a28(undriven_34[28]), .a29(undriven_34[29]),
    .a30(undriven_34[30]), .a31(undriven_34[31]), .W_En(undriven_18), .CLK(undriven_5),
    .s0(registrador_5_s0[0]), .s1(registrador_5_s0[1]), .s2(registrador_5_s0[2]), .s3(registrador_5_s0[3]),
    .s4(registrador_5_s0[4]), .s5(registrador_5_s0[5]), .s6(registrador_5_s0[6]), .s7(registrador_5_s0[7]),
    .s8(registrador_5_s0[8]), .s9(registrador_5_s0[9]), .s10(registrador_5_s0[10]),
    .s11(registrador_5_s0[11]), .s12(registrador_5_s0[12]), .s13(registrador_5_s0[13]),
    .s14(registrador_5_s0[14]), .s15(registrador_5_s0[15]), .s16(registrador_5_s0[16]),
    .s17(registrador_5_s0[17]), .s18(registrador_5_s0[18]), .s19(registrador_5_s0[19]),
    .s20(registrador_5_s0[20]), .s21(registrador_5_s0[21]), .s22(registrador_5_s0[22]),
    .s23(registrador_5_s0[23]), .s24(registrador_5_s0[24]), .s25(registrador_5_s0[25]),
    .s26(registrador_5_s0[26]), .s27(registrador_5_s0[27]), .s28(registrador_5_s0[28]),
    .s29(registrador_5_s0[29]), .s30(registrador_5_s0[30]), .s31(registrador_5_s0[31]));
  Registrador registrador_6 (
    .a0(undriven_35[0]), .a1(undriven_35[1]), .a2(undriven_35[2]), .a3(undriven_35[3]), .a4(undriven_35[4]),
    .a5(undriven_35[5]), .a6(undriven_35[6]), .a7(undriven_35[7]), .a8(undriven_35[8]), .a9(undriven_35[9]),
    .a10(undriven_35[10]), .a11(undriven_35[11]), .a12(undriven_35[12]), .a13(undriven_35[13]),
    .a14(undriven_35[14]), .a15(undriven_35[15]), .a16(undriven_35[16]), .a17(undriven_35[17]),
    .a18(undriven_35[18]), .a19(undriven_35[19]), .a20(undriven_35[20]), .a21(undriven_35[21]),
    .a22(undriven_35[22]), .a23(undriven_35[23]), .a24(undriven_35[24]), .a25(undriven_35[25]),
    .a26(undriven_35[26]), .a27(undriven_35[27]), .a28(undriven_35[28]), .a29(undriven_35[29]),
    .a30(undriven_35[30]), .a31(undriven_35[31]), .W_En(undriven_19), .CLK(undriven_6),
    .s0(registrador_6_s0[0]), .s1(registrador_6_s0[1]), .s2(registrador_6_s0[2]), .s3(registrador_6_s0[3]),
    .s4(registrador_6_s0[4]), .s5(registrador_6_s0[5]), .s6(registrador_6_s0[6]), .s7(registrador_6_s0[7]),
    .s8(registrador_6_s0[8]), .s9(registrador_6_s0[9]), .s10(registrador_6_s0[10]),
    .s11(registrador_6_s0[11]), .s12(registrador_6_s0[12]), .s13(registrador_6_s0[13]),
    .s14(registrador_6_s0[14]), .s15(registrador_6_s0[15]), .s16(registrador_6_s0[16]),
    .s17(registrador_6_s0[17]), .s18(registrador_6_s0[18]), .s19(registrador_6_s0[19]),
    .s20(registrador_6_s0[20]), .s21(registrador_6_s0[21]), .s22(registrador_6_s0[22]),
    .s23(registrador_6_s0[23]), .s24(registrador_6_s0[24]), .s25(registrador_6_s0[25]),
    .s26(registrador_6_s0[26]), .s27(registrador_6_s0[27]), .s28(registrador_6_s0[28]),
    .s29(registrador_6_s0[29]), .s30(registrador_6_s0[30]), .s31(registrador_6_s0[31]));
  Registrador registrador_7 (
    .a0(undriven_36[0]), .a1(undriven_36[1]), .a2(undriven_36[2]), .a3(undriven_36[3]), .a4(undriven_36[4]),
    .a5(undriven_36[5]), .a6(undriven_36[6]), .a7(undriven_36[7]), .a8(undriven_36[8]), .a9(undriven_36[9]),
    .a10(undriven_36[10]), .a11(undriven_36[11]), .a12(undriven_36[12]), .a13(undriven_36[13]),
    .a14(undriven_36[14]), .a15(undriven_36[15]), .a16(undriven_36[16]), .a17(undriven_36[17]),
    .a18(undriven_36[18]), .a19(undriven_36[19]), .a20(undriven_36[20]), .a21(undriven_36[21]),
    .a22(undriven_36[22]), .a23(undriven_36[23]), .a24(undriven_36[24]), .a25(undriven_36[25]),
    .a26(undriven_36[26]), .a27(undriven_36[27]), .a28(undriven_36[28]), .a29(undriven_36[29]),
    .a30(undriven_36[30]), .a31(undriven_36[31]), .W_En(undriven_20), .CLK(undriven_7),
    .s0(registrador_7_s0[0]), .s1(registrador_7_s0[1]), .s2(registrador_7_s0[2]), .s3(registrador_7_s0[3]),
    .s4(registrador_7_s0[4]), .s5(registrador_7_s0[5]), .s6(registrador_7_s0[6]), .s7(registrador_7_s0[7]),
    .s8(registrador_7_s0[8]), .s9(registrador_7_s0[9]), .s10(registrador_7_s0[10]),
    .s11(registrador_7_s0[11]), .s12(registrador_7_s0[12]), .s13(registrador_7_s0[13]),
    .s14(registrador_7_s0[14]), .s15(registrador_7_s0[15]), .s16(registrador_7_s0[16]),
    .s17(registrador_7_s0[17]), .s18(registrador_7_s0[18]), .s19(registrador_7_s0[19]),
    .s20(registrador_7_s0[20]), .s21(registrador_7_s0[21]), .s22(registrador_7_s0[22]),
    .s23(registrador_7_s0[23]), .s24(registrador_7_s0[24]), .s25(registrador_7_s0[25]),
    .s26(registrador_7_s0[26]), .s27(registrador_7_s0[27]), .s28(registrador_7_s0[28]),
    .s29(registrador_7_s0[29]), .s30(registrador_7_s0[30]), .s31(registrador_7_s0[31]));
  Registrador registrador_8 (
    .a0(undriven_37[0]), .a1(undriven_37[1]), .a2(undriven_37[2]), .a3(undriven_37[3]), .a4(undriven_37[4]),
    .a5(undriven_37[5]), .a6(undriven_37[6]), .a7(undriven_37[7]), .a8(undriven_37[8]), .a9(undriven_37[9]),
    .a10(undriven_37[10]), .a11(undriven_37[11]), .a12(undriven_37[12]), .a13(undriven_37[13]),
    .a14(undriven_37[14]), .a15(undriven_37[15]), .a16(undriven_37[16]), .a17(undriven_37[17]),
    .a18(undriven_37[18]), .a19(undriven_37[19]), .a20(undriven_37[20]), .a21(undriven_37[21]),
    .a22(undriven_37[22]), .a23(undriven_37[23]), .a24(undriven_37[24]), .a25(undriven_37[25]),
    .a26(undriven_37[26]), .a27(undriven_37[27]), .a28(undriven_37[28]), .a29(undriven_37[29]),
    .a30(undriven_37[30]), .a31(undriven_37[31]), .W_En(undriven_21), .CLK(undriven_8),
    .s0(registrador_8_s0[0]), .s1(registrador_8_s0[1]), .s2(registrador_8_s0[2]), .s3(registrador_8_s0[3]),
    .s4(registrador_8_s0[4]), .s5(registrador_8_s0[5]), .s6(registrador_8_s0[6]), .s7(registrador_8_s0[7]),
    .s8(registrador_8_s0[8]), .s9(registrador_8_s0[9]), .s10(registrador_8_s0[10]),
    .s11(registrador_8_s0[11]), .s12(registrador_8_s0[12]), .s13(registrador_8_s0[13]),
    .s14(registrador_8_s0[14]), .s15(registrador_8_s0[15]), .s16(registrador_8_s0[16]),
    .s17(registrador_8_s0[17]), .s18(registrador_8_s0[18]), .s19(registrador_8_s0[19]),
    .s20(registrador_8_s0[20]), .s21(registrador_8_s0[21]), .s22(registrador_8_s0[22]),
    .s23(registrador_8_s0[23]), .s24(registrador_8_s0[24]), .s25(registrador_8_s0[25]),
    .s26(registrador_8_s0[26]), .s27(registrador_8_s0[27]), .s28(registrador_8_s0[28]),
    .s29(registrador_8_s0[29]), .s30(registrador_8_s0[30]), .s31(registrador_8_s0[31]));
  Registrador registrador_9 (
    .a0(undriven_38[0]), .a1(undriven_38[1]), .a2(undriven_38[2]), .a3(undriven_38[3]), .a4(undriven_38[4]),
    .a5(undriven_38[5]), .a6(undriven_38[6]), .a7(undriven_38[7]), .a8(undriven_38[8]), .a9(undriven_38[9]),
    .a10(undriven_38[10]), .a11(undriven_38[11]), .a12(undriven_38[12]), .a13(undriven_38[13]),
    .a14(undriven_38[14]), .a15(undriven_38[15]), .a16(undriven_38[16]), .a17(undriven_38[17]),
    .a18(undriven_38[18]), .a19(undriven_38[19]), .a20(undriven_38[20]), .a21(undriven_38[21]),
    .a22(undriven_38[22]), .a23(undriven_38[23]), .a24(undriven_38[24]), .a25(undriven_38[25]),
    .a26(undriven_38[26]), .a27(undriven_38[27]), .a28(undriven_38[28]), .a29(undriven_38[29]),
    .a30(undriven_38[30]), .a31(undriven_38[31]), .W_En(undriven_22), .CLK(undriven_9),
    .s0(registrador_9_s0[0]), .s1(registrador_9_s0[1]), .s2(registrador_9_s0[2]), .s3(registrador_9_s0[3]),
    .s4(registrador_9_s0[4]), .s5(registrador_9_s0[5]), .s6(registrador_9_s0[6]), .s7(registrador_9_s0[7]),
    .s8(registrador_9_s0[8]), .s9(registrador_9_s0[9]), .s10(registrador_9_s0[10]),
    .s11(registrador_9_s0[11]), .s12(registrador_9_s0[12]), .s13(registrador_9_s0[13]),
    .s14(registrador_9_s0[14]), .s15(registrador_9_s0[15]), .s16(registrador_9_s0[16]),
    .s17(registrador_9_s0[17]), .s18(registrador_9_s0[18]), .s19(registrador_9_s0[19]),
    .s20(registrador_9_s0[20]), .s21(registrador_9_s0[21]), .s22(registrador_9_s0[22]),
    .s23(registrador_9_s0[23]), .s24(registrador_9_s0[24]), .s25(registrador_9_s0[25]),
    .s26(registrador_9_s0[26]), .s27(registrador_9_s0[27]), .s28(registrador_9_s0[28]),
    .s29(registrador_9_s0[29]), .s30(registrador_9_s0[30]), .s31(registrador_9_s0[31]));
  Registrador registrador_10 (
    .a0(undriven_39[0]), .a1(undriven_39[1]), .a2(undriven_39[2]), .a3(undriven_39[3]), .a4(undriven_39[4]),
    .a5(undriven_39[5]), .a6(undriven_39[6]), .a7(undriven_39[7]), .a8(undriven_39[8]), .a9(undriven_39[9]),
    .a10(undriven_39[10]), .a11(undriven_39[11]), .a12(undriven_39[12]), .a13(undriven_39[13]),
    .a14(undriven_39[14]), .a15(undriven_39[15]), .a16(undriven_39[16]), .a17(undriven_39[17]),
    .a18(undriven_39[18]), .a19(undriven_39[19]), .a20(undriven_39[20]), .a21(undriven_39[21]),
    .a22(undriven_39[22]), .a23(undriven_39[23]), .a24(undriven_39[24]), .a25(undriven_39[25]),
    .a26(undriven_39[26]), .a27(undriven_39[27]), .a28(undriven_39[28]), .a29(undriven_39[29]),
    .a30(undriven_39[30]), .a31(undriven_39[31]), .W_En(undriven_23), .CLK(undriven_10),
    .s0(registrador_10_s0[0]), .s1(registrador_10_s0[1]), .s2(registrador_10_s0[2]),
    .s3(registrador_10_s0[3]), .s4(registrador_10_s0[4]), .s5(registrador_10_s0[5]),
    .s6(registrador_10_s0[6]), .s7(registrador_10_s0[7]), .s8(registrador_10_s0[8]),
    .s9(registrador_10_s0[9]), .s10(registrador_10_s0[10]), .s11(registrador_10_s0[11]),
    .s12(registrador_10_s0[12]), .s13(registrador_10_s0[13]), .s14(registrador_10_s0[14]),
    .s15(registrador_10_s0[15]), .s16(registrador_10_s0[16]), .s17(registrador_10_s0[17]),
    .s18(registrador_10_s0[18]), .s19(registrador_10_s0[19]), .s20(registrador_10_s0[20]),
    .s21(registrador_10_s0[21]), .s22(registrador_10_s0[22]), .s23(registrador_10_s0[23]),
    .s24(registrador_10_s0[24]), .s25(registrador_10_s0[25]), .s26(registrador_10_s0[26]),
    .s27(registrador_10_s0[27]), .s28(registrador_10_s0[28]), .s29(registrador_10_s0[29]),
    .s30(registrador_10_s0[30]), .s31(registrador_10_s0[31]));
  Registrador registrador_11 (
    .a0(undriven_40[0]), .a1(undriven_40[1]), .a2(undriven_40[2]), .a3(undriven_40[3]), .a4(undriven_40[4]),
    .a5(undriven_40[5]), .a6(undriven_40[6]), .a7(undriven_40[7]), .a8(undriven_40[8]), .a9(undriven_40[9]),
    .a10(undriven_40[10]), .a11(undriven_40[11]), .a12(undriven_40[12]), .a13(undriven_40[13]),
    .a14(undriven_40[14]), .a15(undriven_40[15]), .a16(undriven_40[16]), .a17(undriven_40[17]),
    .a18(undriven_40[18]), .a19(undriven_40[19]), .a20(undriven_40[20]), .a21(undriven_40[21]),
    .a22(undriven_40[22]), .a23(undriven_40[23]), .a24(undriven_40[24]), .a25(undriven_40[25]),
    .a26(undriven_40[26]), .a27(undriven_40[27]), .a28(undriven_40[28]), .a29(undriven_40[29]),
    .a30(undriven_40[30]), .a31(undriven_40[31]), .W_En(undriven_24), .CLK(undriven_11),
    .s0(registrador_11_s0[0]), .s1(registrador_11_s0[1]), .s2(registrador_11_s0[2]),
    .s3(registrador_11_s0[3]), .s4(registrador_11_s0[4]), .s5(registrador_11_s0[5]),
    .s6(registrador_11_s0[6]), .s7(registrador_11_s0[7]), .s8(registrador_11_s0[8]),
    .s9(registrador_11_s0[9]), .s10(registrador_11_s0[10]), .s11(registrador_11_s0[11]),
    .s12(registrador_11_s0[12]), .s13(registrador_11_s0[13]), .s14(registrador_11_s0[14]),
    .s15(registrador_11_s0[15]), .s16(registrador_11_s0[16]), .s17(registrador_11_s0[17]),
    .s18(registrador_11_s0[18]), .s19(registrador_11_s0[19]), .s20(registrador_11_s0[20]),
    .s21(registrador_11_s0[21]), .s22(registrador_11_s0[22]), .s23(registrador_11_s0[23]),
    .s24(registrador_11_s0[24]), .s25(registrador_11_s0[25]), .s26(registrador_11_s0[26]),
    .s27(registrador_11_s0[27]), .s28(registrador_11_s0[28]), .s29(registrador_11_s0[29]),
    .s30(registrador_11_s0[30]), .s31(registrador_11_s0[31]));
  Registrador registrador_12 (
    .a0(undriven_41[0]), .a1(undriven_41[1]), .a2(undriven_41[2]), .a3(undriven_41[3]), .a4(undriven_41[4]),
    .a5(undriven_41[5]), .a6(undriven_41[6]), .a7(undriven_41[7]), .a8(undriven_41[8]), .a9(undriven_41[9]),
    .a10(undriven_41[10]), .a11(undriven_41[11]), .a12(undriven_41[12]), .a13(undriven_41[13]),
    .a14(undriven_41[14]), .a15(undriven_41[15]), .a16(undriven_41[16]), .a17(undriven_41[17]),
    .a18(undriven_41[18]), .a19(undriven_41[19]), .a20(undriven_41[20]), .a21(undriven_41[21]),
    .a22(undriven_41[22]), .a23(undriven_41[23]), .a24(undriven_41[24]), .a25(undriven_41[25]),
    .a26(undriven_41[26]), .a27(undriven_41[27]), .a28(undriven_41[28]), .a29(undriven_41[29]),
    .a30(undriven_41[30]), .a31(undriven_41[31]), .W_En(undriven_25), .CLK(undriven_12),
    .s0(registrador_12_s0[0]), .s1(registrador_12_s0[1]), .s2(registrador_12_s0[2]),
    .s3(registrador_12_s0[3]), .s4(registrador_12_s0[4]), .s5(registrador_12_s0[5]),
    .s6(registrador_12_s0[6]), .s7(registrador_12_s0[7]), .s8(registrador_12_s0[8]),
    .s9(registrador_12_s0[9]), .s10(registrador_12_s0[10]), .s11(registrador_12_s0[11]),
    .s12(registrador_12_s0[12]), .s13(registrador_12_s0[13]), .s14(registrador_12_s0[14]),
    .s15(registrador_12_s0[15]), .s16(registrador_12_s0[16]), .s17(registrador_12_s0[17]),
    .s18(registrador_12_s0[18]), .s19(registrador_12_s0[19]), .s20(registrador_12_s0[20]),
    .s21(registrador_12_s0[21]), .s22(registrador_12_s0[22]), .s23(registrador_12_s0[23]),
    .s24(registrador_12_s0[24]), .s25(registrador_12_s0[25]), .s26(registrador_12_s0[26]),
    .s27(registrador_12_s0[27]), .s28(registrador_12_s0[28]), .s29(registrador_12_s0[29]),
    .s30(registrador_12_s0[30]), .s31(registrador_12_s0[31]));
  Registrador registrador_13 (
    .a0(undriven_42[0]), .a1(undriven_42[1]), .a2(undriven_42[2]), .a3(undriven_42[3]), .a4(undriven_42[4]),
    .a5(undriven_42[5]), .a6(undriven_42[6]), .a7(undriven_42[7]), .a8(undriven_42[8]), .a9(undriven_42[9]),
    .a10(undriven_42[10]), .a11(undriven_42[11]), .a12(undriven_42[12]), .a13(undriven_42[13]),
    .a14(undriven_42[14]), .a15(undriven_42[15]), .a16(undriven_42[16]), .a17(undriven_42[17]),
    .a18(undriven_42[18]), .a19(undriven_42[19]), .a20(undriven_42[20]), .a21(undriven_42[21]),
    .a22(undriven_42[22]), .a23(undriven_42[23]), .a24(undriven_42[24]), .a25(undriven_42[25]),
    .a26(undriven_42[26]), .a27(undriven_42[27]), .a28(undriven_42[28]), .a29(undriven_42[29]),
    .a30(undriven_42[30]), .a31(undriven_42[31]), .W_En(undriven_26), .CLK(undriven_13),
    .s0(registrador_13_s0[0]), .s1(registrador_13_s0[1]), .s2(registrador_13_s0[2]),
    .s3(registrador_13_s0[3]), .s4(registrador_13_s0[4]), .s5(registrador_13_s0[5]),
    .s6(registrador_13_s0[6]), .s7(registrador_13_s0[7]), .s8(registrador_13_s0[8]),
    .s9(registrador_13_s0[9]), .s10(registrador_13_s0[10]), .s11(registrador_13_s0[11]),
    .s12(registrador_13_s0[12]), .s13(registrador_13_s0[13]), .s14(registrador_13_s0[14]),
    .s15(registrador_13_s0[15]), .s16(registrador_13_s0[16]), .s17(registrador_13_s0[17]),
    .s18(registrador_13_s0[18]), .s19(registrador_13_s0[19]), .s20(registrador_13_s0[20]),
    .s21(registrador_13_s0[21]), .s22(registrador_13_s0[22]), .s23(registrador_13_s0[23]),
    .s24(registrador_13_s0[24]), .s25(registrador_13_s0[25]), .s26(registrador_13_s0[26]),
    .s27(registrador_13_s0[27]), .s28(registrador_13_s0[28]), .s29(registrador_13_s0[29]),
    .s30(registrador_13_s0[30]), .s31(registrador_13_s0[31]));
  Registrador registrador_14 (
    .a0(undriven_43[0]), .a1(undriven_43[1]), .a2(undriven_43[2]), .a3(undriven_43[3]), .a4(undriven_43[4]),
    .a5(undriven_43[5]), .a6(undriven_43[6]), .a7(undriven_43[7]), .a8(undriven_43[8]), .a9(undriven_43[9]),
    .a10(undriven_43[10]), .a11(undriven_43[11]), .a12(undriven_43[12]), .a13(undriven_43[13]),
    .a14(undriven_43[14]), .a15(undriven_43[15]), .a16(undriven_43[16]), .a17(undriven_43[17]),
    .a18(undriven_43[18]), .a19(undriven_43[19]), .a20(undriven_43[20]), .a21(undriven_43[21]),
    .a22(undriven_43[22]), .a23(undriven_43[23]), .a24(undriven_43[24]), .a25(undriven_43[25]),
    .a26(undriven_43[26]), .a27(undriven_43[27]), .a28(undriven_43[28]), .a29(undriven_43[29]),
    .a30(undriven_43[30]), .a31(undriven_43[31]), .W_En(undriven_27), .CLK(undriven_14),
    .s0(registrador_14_s0[0]), .s1(registrador_14_s0[1]), .s2(registrador_14_s0[2]),
    .s3(registrador_14_s0[3]), .s4(registrador_14_s0[4]), .s5(registrador_14_s0[5]),
    .s6(registrador_14_s0[6]), .s7(registrador_14_s0[7]), .s8(registrador_14_s0[8]),
    .s9(registrador_14_s0[9]), .s10(registrador_14_s0[10]), .s11(registrador_14_s0[11]),
    .s12(registrador_14_s0[12]), .s13(registrador_14_s0[13]), .s14(registrador_14_s0[14]),
    .s15(registrador_14_s0[15]), .s16(registrador_14_s0[16]), .s17(registrador_14_s0[17]),
    .s18(registrador_14_s0[18]), .s19(registrador_14_s0[19]), .s20(registrador_14_s0[20]),
    .s21(registrador_14_s0[21]), .s22(registrador_14_s0[22]), .s23(registrador_14_s0[23]),
    .s24(registrador_14_s0[24]), .s25(registrador_14_s0[25]), .s26(registrador_14_s0[26]),
    .s27(registrador_14_s0[27]), .s28(registrador_14_s0[28]), .s29(registrador_14_s0[29]),
    .s30(registrador_14_s0[30]), .s31(registrador_14_s0[31]));
  Registrador registrador_15 (
    .a0(undriven_44[0]), .a1(undriven_44[1]), .a2(undriven_44[2]), .a3(undriven_44[3]), .a4(undriven_44[4]),
    .a5(undriven_44[5]), .a6(undriven_44[6]), .a7(undriven_44[7]), .a8(undriven_44[8]), .a9(undriven_44[9]),
    .a10(undriven_44[10]), .a11(undriven_44[11]), .a12(undriven_44[12]), .a13(undriven_44[13]),
    .a14(undriven_44[14]), .a15(undriven_44[15]), .a16(undriven_44[16]), .a17(undriven_44[17]),
    .a18(undriven_44[18]), .a19(undriven_44[19]), .a20(undriven_44[20]), .a21(undriven_44[21]),
    .a22(undriven_44[22]), .a23(undriven_44[23]), .a24(undriven_44[24]), .a25(undriven_44[25]),
    .a26(undriven_44[26]), .a27(undriven_44[27]), .a28(undriven_44[28]), .a29(undriven_44[29]),
    .a30(undriven_44[30]), .a31(undriven_44[31]), .W_En(undriven_28), .CLK(undriven_15),
    .s0(registrador_15_s0[0]), .s1(registrador_15_s0[1]), .s2(registrador_15_s0[2]),
    .s3(registrador_15_s0[3]), .s4(registrador_15_s0[4]), .s5(registrador_15_s0[5]),
    .s6(registrador_15_s0[6]), .s7(registrador_15_s0[7]), .s8(registrador_15_s0[8]),
    .s9(registrador_15_s0[9]), .s10(registrador_15_s0[10]), .s11(registrador_15_s0[11]),
    .s12(registrador_15_s0[12]), .s13(registrador_15_s0[13]), .s14(registrador_15_s0[14]),
    .s15(registrador_15_s0[15]), .s16(registrador_15_s0[16]), .s17(registrador_15_s0[17]),
    .s18(registrador_15_s0[18]), .s19(registrador_15_s0[19]), .s20(registrador_15_s0[20]),
    .s21(registrador_15_s0[21]), .s22(registrador_15_s0[22]), .s23(registrador_15_s0[23]),
    .s24(registrador_15_s0[24]), .s25(registrador_15_s0[25]), .s26(registrador_15_s0[26]),
    .s27(registrador_15_s0[27]), .s28(registrador_15_s0[28]), .s29(registrador_15_s0[29]),
    .s30(registrador_15_s0[30]), .s31(registrador_15_s0[31]));
  Registrador registrador_16 (
    .a0(undriven_45[0]), .a1(undriven_45[1]), .a2(undriven_45[2]), .a3(undriven_45[3]), .a4(undriven_45[4]),
    .a5(undriven_45[5]), .a6(undriven_45[6]), .a7(undriven_45[7]), .a8(undriven_45[8]), .a9(undriven_45[9]),
    .a10(undriven_45[10]), .a11(undriven_45[11]), .a12(undriven_45[12]), .a13(undriven_45[13]),
    .a14(undriven_45[14]), .a15(undriven_45[15]), .a16(undriven_45[16]), .a17(undriven_45[17]),
    .a18(undriven_45[18]), .a19(undriven_45[19]), .a20(undriven_45[20]), .a21(undriven_45[21]),
    .a22(undriven_45[22]), .a23(undriven_45[23]), .a24(undriven_45[24]), .a25(undriven_45[25]),
    .a26(undriven_45[26]), .a27(undriven_45[27]), .a28(undriven_45[28]), .a29(undriven_45[29]),
    .a30(undriven_45[30]), .a31(undriven_45[31]), .W_En(undriven_29), .CLK(CLK), .s0(registrador_16_s0[0]),
    .s1(registrador_16_s0[1]), .s2(registrador_16_s0[2]), .s3(registrador_16_s0[3]),
    .s4(registrador_16_s0[4]), .s5(registrador_16_s0[5]), .s6(registrador_16_s0[6]),
    .s7(registrador_16_s0[7]), .s8(registrador_16_s0[8]), .s9(registrador_16_s0[9]),
    .s10(registrador_16_s0[10]), .s11(registrador_16_s0[11]), .s12(registrador_16_s0[12]),
    .s13(registrador_16_s0[13]), .s14(registrador_16_s0[14]), .s15(registrador_16_s0[15]),
    .s16(registrador_16_s0[16]), .s17(registrador_16_s0[17]), .s18(registrador_16_s0[18]),
    .s19(registrador_16_s0[19]), .s20(registrador_16_s0[20]), .s21(registrador_16_s0[21]),
    .s22(registrador_16_s0[22]), .s23(registrador_16_s0[23]), .s24(registrador_16_s0[24]),
    .s25(registrador_16_s0[25]), .s26(registrador_16_s0[26]), .s27(registrador_16_s0[27]),
    .s28(registrador_16_s0[28]), .s29(registrador_16_s0[29]), .s30(registrador_16_s0[30]),
    .s31(registrador_16_s0[31]));
  Multiplexer #(.select(4), .width(32)) multiplexer_1 ();  // open: in0, in1, in2, in3, in4, in5, in6, in7, in8, in9, in10, in11, in12, in13, in14, in15, out, sel
  Multiplexer #(.select(4), .width(32)) multiplexer_2 (.in15(registrador_16_s0));  // open: in0, in1, in2, in3, in4, in5, in6, in7, in8, in9, in10, in11, in12, in13, in14, out, sel
endmodule
